// Logisim project project.circ as structural Verilog: 1 circuit, main circuit main
module main (
  input  in_1,
  input  in_2,
  input  [2:0] in_3,
  input  in_4,
  input  [2:0] in_5,
  input  in_6,
  input  in_7,
  input  write,
  input  read
);

  wire clock_1_out, undriven, undriven_2;
  wire [6:0] AR_q, bit_extender_1_out;
  wire [15:0] AC_q, adder_1_out, adder_2_out, and_1_out, bit_extender_2_out, DR_q, multiplexer_1_out,
       multiplexer_2_out, multiplier_1_out, or_1_out, ram_1_data, subtractor_1_out, TR_q;

  Adder #(.width(16)) adder_1 (.a(DR_q), .b(AC_q), .out(adder_1_out));  // open: cin, cout
  Subtractor #(.width(16)) subtractor_1 (.a(DR_q), .b(AC_q), .out(subtractor_1_out));  // open: bin, bout
  Multiplier #(.width(16)) multiplier_1 (.a(DR_q), .b(AC_q), .out(multiplier_1_out));  // open: cin, cout
  Adder #(.width(16)) adder_2 (.a(DR_q), .b(16'h1), .out(adder_2_out));  // open: cin, cout
  assign or_1_out = DR_q | AC_q;  // OR_Gate or_1, 16 bits wide
  assign and_1_out = DR_q & AC_q;  // AND_Gate and_1, 16 bits wide
  Multiplexer #(.select(3), .width(16), .enable("false")) multiplexer_1 (
    .in1(DR_q), .in2(adder_1_out), .in3(subtractor_1_out), .in4(multiplier_1_out), .in5(adder_2_out),
    .in6(or_1_out), .in7(and_1_out), .out(multiplexer_1_out), .sel(in_3));  // open: in0
  Bit_Extender #(.in_width(16), .out_width(7)) bit_extender_1 (.in(multiplexer_2_out), .out(bit_extender_1_out));
  Clock clock_1 (.out(clock_1_out));
  Register #(.width(16)) AC (.D(multiplexer_1_out), .en(in_1), .Q(AC_q), .clk(clock_1_out));  // open: clr
  Register #(.width(16)) DR (.D(multiplexer_2_out), .en(in_2), .Q(DR_q), .clk(clock_1_out));  // open: clr
  Register #(.width(16)) TR (.D(multiplexer_2_out), .en(in_4), .Q(TR_q), .clk(clock_1_out));  // open: clr
  Register #(.width(7)) AR (.D(bit_extender_1_out), .en(in_6), .Q(AR_q), .clk(clock_1_out));  // open: clr
  RAM #(.addrWidth(7), .dataWidth(16), .bus("separate")) ram_1 (
    .addr(AR_q), .din(multiplexer_2_out), .data(ram_1_data), .str(undriven), .sel(in_7), .clk(clock_1_out),
    .ld(undriven_2));  // open: clr
  assign bit_extender_2_out = {{9{1'b0}}, AR_q};  // Bit_Extender bit_extender_2
  Multiplexer #(.select(3), .width(16)) multiplexer_2 (
    .in0(AC_q), .in1(DR_q), .in2(TR_q), .in3(bit_extender_2_out), .in4(ram_1_data), .out(multiplexer_2_out),
    .sel(in_5));  // open: in5, in6, in7, en
endmodule
